// Logisim project BigASM.circ as structural Verilog
module BOARD_BIG_ASM (
  output out_1
);

  wire button_1_out, CLK, CLR, d_ff_1_q, not_1_out, Write, Write_ASCII;
  wire [6:0] ASCII;
  wire [7:0] counter_1_q;
  wire [23:0] Dir_INPUT, Dir_MEMORY;
  wire [31:0] INPUT, MEMORY_IN, MEMORY_OUT;

  Button button_1 (.out(button_1_out));
  Clock clock_1 (.out(CLK));
  D_Flip_Flop d_ff_1 (.clk(CLK), .D(1'b1), .Q(d_ff_1_q), .reset(button_1_out));  // open: Qn, preset, en
  D_Flip_Flop d_ff_2 (.clk(CLK), .D(d_ff_1_q), .Qn(CLR), .reset(button_1_out));  // open: Q, preset, en
  BIG_ASM big_asm_1 (
    .DATA_INPUT(INPUT), .MEMORY_IN(MEMORY_OUT), .CLK(CLK), .CLR(CLR), .DIR_INPUT(Dir_INPUT),
    .MEMORY_OUT(MEMORY_IN), .DIR_MEMORY(Dir_MEMORY), .Write_OUTPUT(Write), .ASCII(ASCII),
    .Write_ASCII(Write_ASCII), .END(out_1));
  MEMORY memory_1 (.DIR(Dir_MEMORY), .DATA_IN(MEMORY_IN), .WRITE(Write), .CLK(CLK), .CLR(CLR), .DATA_OUT(MEMORY_OUT));
  INPUT input_1 (.DIR(Dir_INPUT), .CLK(CLK), .DATA_OUT(INPUT));
  Counter counter_1 (.load(1'b0), .count(not_1_out), .Q(counter_1_q), .clk(CLK), .clr(CLR));  // open: D, carry
  not not_1 (not_1_out, out_1);
  // Probe on counter_1_q
  TTY #(.rows(32), .cols(60)) tty_1 (.data(ASCII), .clk(CLK), .we(Write_ASCII), .clr(CLR));

  // Other names for the same wires on the sheet: END = out_1

  // Notes on the sheet:
  //   COUNTER
  //   BOARD
endmodule

module INPUT (
  input  [23:0] DIR,
  input  CLK,
  output [31:0] DATA_OUT
);

  RAM #(.addrWidth(24), .dataWidth(32)) ram_1 (.addr(DIR), .data(DATA_OUT), .clk(CLK), .ld(1'b1));  // open: sel, clr
endmodule

module MEMORY (
  input  [23:0] DIR,
  input  [31:0] DATA_IN,
  input  WRITE,
  input  CLK,
  input  CLR,
  output [31:0] DATA_OUT
);

  RAM #(.addrWidth(24), .dataWidth(32), .bus("separate")) ram_1 (
    .addr(DIR), .din(DATA_IN), .data(DATA_OUT), .str(WRITE), .clk(CLK), .clr(CLR));  // open: sel, ld
endmodule

module BIG_ASM (
  input  [31:0] DATA_INPUT,
  input  [31:0] MEMORY_IN,
  input  CLK,
  input  CLR,
  output [23:0] DIR_INPUT,
  output [31:0] MEMORY_OUT,
  output [23:0] DIR_MEMORY,
  output Write_OUTPUT,
  output [6:0] ASCII,
  output Write_ASCII,
  output END
);

  wire A__B, d_ff_1_q, i__A, j__A_B_1, j__A_B_1_t, Key___Input__j, LA, LB, Li, Lj, LKey, Output, Si, Sj,
       Start;
  wire [23:0] Dir_Input_t;

  D_Flip_Flop d_ff_1 (.clk(CLK), .D(1'b0), .Q(d_ff_1_q), .preset(CLR));  // open: Qn, en, reset
  D_Flip_Flop d_ff_2 (.clk(CLK), .D(d_ff_1_q), .Q(Start), .reset(CLR));  // open: Qn, preset, en
  C_U c_u_1 (
    .in_1(Start), .in_2(A__B), .in_3(i__A), .in_5(j__A_B_1_t), .Load_A(LA), .Load_B(LB), .Load_i(Li),
    .Select_i(Si), .Load_Key(LKey), .Load_j(Lj), .Select_j(Sj), .END(END), .Output(Output), .in_7(CLK),
    .in_6(j__A_B_1), .in_8(CLR), .in_4(Key___Input__j));
  D_P d_p_1 (
    .in_4(Si), .in_3(Li), .in_7(Sj), .in_6(Lj), .in_1(LA), .in_2(LB), .in_8(DATA_INPUT), .in_9(CLK),
    .out_14(j__A_B_1_t), .out_11(A__B), .out_12(i__A), .in_5(LKey), .out_13(Key___Input__j),
    .Dir_Input(Dir_Input_t), .in_10(CLR), .out_15(j__A_B_1));
  Multiplexer #(.width(24), .enable("false")) multiplexer_1 (
    .in0(Dir_Input_t), .in1({24{1'b0}}), .out(DIR_INPUT), .sel(CLR));
  Multiplexer #(.width(7), .enable("false")) multiplexer_2 (
    .in0(7'b0110000), .in1(7'b0110001), .out(ASCII), .sel(Output));

  assign DIR_MEMORY = {24{1'b0}};
  assign MEMORY_OUT = {32{1'b0}};
  assign Write_ASCII = END;
  assign Write_OUTPUT = 1'b0;

  // Other names for the same wires on the sheet: DI[31:0] = DATA_INPUT; MI[31:0] = MEMORY_IN
endmodule

module PRINT_UDEC (
  input  [31:0] num,
  input  start,
  input  CLK,
  input  RST,
  output [6:0] ASCII,
  output Write_ASCII,
  output \end 
);

  wire _0_c, _0_n, demultiplexer_1_out0, demultiplexer_2_out0, demultiplexer_2_out1, demultiplexer_3_out0,
       demultiplexer_3_out1, IDLE_2_q, IDLE_3_q, IDLE_4_q, IDLE_q, Lc, Lc_0, Ln, Ln_0, or_1_out;
  wire [23:0] bit_extender_1_out;
  wire [31:0] c, c___1, c___1_t, divider_1_rem, memory_1_data_out, multiplexer_1_out, multiplexer_2_out,
       multiplexer_3_out, n, n___10, n___10___48;

  Multiplexer #(.width(32), .enable("false")) multiplexer_1 (
    .in0(num), .in1(n___10), .out(multiplexer_1_out), .sel(Lc_0));
  Divider #(.width(32)) divider_1 (.a(n), .b(32'ha), .out(n___10), .rem(divider_1_rem));  // open: upper
  Adder #(.width(32)) adder_1 (.a(divider_1_rem), .b(32'h30), .out(n___10___48));  // open: cin, cout
  or or_1 (or_1_out, demultiplexer_1_out0, \end );
  Register #(.width(32)) u_n (.D(multiplexer_1_out), .en(Ln), .Q(n), .clk(CLK), .clr(RST));
  D_Flip_Flop IDLE (.clk(CLK), .D(or_1_out), .Q(IDLE_q), .preset(RST));  // open: Qn, en, reset
  Demultiplexer #(.enable("false")) demultiplexer_1 (
    .out0(demultiplexer_1_out0), .out1(Ln_0), .in(IDLE_q), .sel(start));
  or or_2 (Write_ASCII, demultiplexer_3_out0, demultiplexer_2_out1);
  Multiplexer #(.width(32), .enable("false")) multiplexer_2 (
    .in0(c___1), .in1(c___1_t), .out(multiplexer_2_out), .sel(Write_ASCII));
  Adder #(.width(32)) adder_2 (.a(c), .b(32'h1), .out(c___1));  // open: cin, cout
  Subtractor #(.width(32)) subtractor_1 (.a(c), .b(32'h1), .out(c___1_t));  // open: bin, bout
  D_Flip_Flop IDLE_2 (.clk(CLK), .D(Ln_0), .Q(IDLE_2_q), .reset(RST));  // open: Qn, preset, en
  Register #(.width(32)) u_c (.D(multiplexer_2_out), .en(Lc), .Q(c), .clk(CLK), .clr(RST));
  or or_3 (Lc_0, IDLE_2_q, demultiplexer_3_out1);
  Multiplexer #(.width(32), .enable("false")) multiplexer_3 (
    .in0(c), .in1(c___1_t), .out(multiplexer_3_out), .sel(Write_ASCII));
  Comparator #(.width(32), .mode("unsigned")) comparator_1 (.a({32{1'b0}}), .b(n), .lt(_0_n));  // open: gt, eq
  Comparator #(.width(32), .mode("unsigned")) comparator_2 (.a({32{1'b0}}), .b(c), .lt(_0_c));  // open: gt, eq
  D_Flip_Flop IDLE_3 (.clk(CLK), .D(Write_ASCII), .Q(IDLE_3_q), .reset(RST));  // open: Qn, preset, en
  Demultiplexer #(.enable("false")) demultiplexer_2 (
    .out0(demultiplexer_2_out0), .out1(demultiplexer_2_out1), .in(IDLE_3_q), .sel(_0_c));
  Bit_Extender #(.in_width(32), .out_width(24)) bit_extender_1 (.in(multiplexer_3_out), .out(bit_extender_1_out));
  D_Flip_Flop IDLE_4 (.clk(CLK), .D(Lc_0), .Q(IDLE_4_q), .reset(RST));  // open: Qn, preset, en
  or or_4 (Lc, Lc_0, Write_ASCII);
  or or_5 (Ln, Ln_0, Lc_0);
  Demultiplexer #(.enable("false")) demultiplexer_3 (
    .out0(demultiplexer_3_out0), .out1(demultiplexer_3_out1), .in(IDLE_4_q), .sel(_0_n));
  D_Flip_Flop IDLE_5 (.clk(CLK), .D(demultiplexer_2_out0), .Q(\end ), .reset(RST));  // open: Qn, preset, en
  MEMORY memory_1 (
    .DIR(bit_extender_1_out), .DATA_IN(n___10___48), .WRITE(Lc_0), .CLK(CLK), .CLR(RST),
    .DATA_OUT(memory_1_data_out));
  Bit_Extender #(.in_width(32), .out_width(7)) bit_extender_2 (.in(memory_1_data_out), .out(ASCII));

  // Other names for the same wires on the sheet: Lc_1 = Write_ASCII; Sc = Write_ASCII; Ln_1 = Lc_0; Sn = Lc_0;
  //   Write = Lc_0
endmodule

module PRINT_DEC (
  input  [31:0] num,
  input  start,
  input  CLK,
  input  RST,
  output [6:0] ASCII,
  output Write_ASCII,
  output END
);

  wire demultiplexer_1_out0, demultiplexer_1_out1, demultiplexer_2_out0, demultiplexer_3_out0, end_t,
       IDLE_3_q, IDLE_q, or_1_out, or_2_out, or_3_out, S_ASCII, startUDEC, Write_ASCII_1;
  wire [6:0] ASCII_t;
  wire [31:0] multiplexer_1_out, negator_1_out;

  or or_1 (or_1_out, demultiplexer_1_out0, END);
  Negator #(.width(32)) negator_1 (.in(num), .out(negator_1_out));
  D_Flip_Flop IDLE (.clk(CLK), .D(or_1_out), .Q(IDLE_q), .preset(RST));  // open: Qn, en, reset
  Demultiplexer #(.enable("false")) demultiplexer_1 (
    .out0(demultiplexer_1_out0), .out1(demultiplexer_1_out1), .in(IDLE_q), .sel(start));
  Multiplexer #(.width(32), .enable("false")) multiplexer_1 (
    .in0(num), .in1(negator_1_out), .out(multiplexer_1_out), .sel(num[31]));
  Demultiplexer #(.enable("false")) demultiplexer_2 (
    .out0(demultiplexer_2_out0), .out1(S_ASCII), .in(demultiplexer_1_out1), .sel(num[31]));
  or or_2 (or_2_out, demultiplexer_2_out0, S_ASCII);
  D_Flip_Flop IDLE_2 (.clk(CLK), .D(or_2_out), .Q(startUDEC), .reset(RST));  // open: Qn, preset, en
  PRINT_UDEC print_udec_1 (
    .num(multiplexer_1_out), .start(startUDEC), .CLK(CLK), .RST(RST), .ASCII(ASCII_t),
    .Write_ASCII(Write_ASCII_1), .\end (end_t));
  D_Flip_Flop IDLE_3 (.clk(CLK), .D(or_3_out), .Q(IDLE_3_q), .reset(RST));  // open: Qn, preset, en
  or or_3 (or_3_out, startUDEC, demultiplexer_3_out0);
  Demultiplexer #(.enable("false")) demultiplexer_3 (
    .out0(demultiplexer_3_out0), .out1(END), .in(IDLE_3_q), .sel(end_t));
  Multiplexer #(.width(7), .enable("false")) multiplexer_2 (
    .in0(ASCII_t), .in1(7'b0101101), .out(ASCII), .sel(S_ASCII));
  or or_4 (Write_ASCII, S_ASCII, Write_ASCII_1);

  // Other names for the same wires on the sheet: sign = num[31]; Write_ASCII_0 = S_ASCII
endmodule

module TEST_PRINT (
  input  [31:0] in_1,
  output out_2
);

  wire button_1_out, button_2_out, CLK, CLR, d_ff_1_q, Write_ASCII;
  wire [6:0] ASCII;

  Button button_1 (.out(button_1_out));
  Clock clock_1 (.out(CLK));
  D_Flip_Flop d_ff_1 (.clk(CLK), .D(1'b1), .Q(d_ff_1_q), .reset(button_1_out));  // open: Qn, preset, en
  D_Flip_Flop d_ff_2 (.clk(CLK), .D(d_ff_1_q), .Qn(CLR), .reset(button_1_out));  // open: Q, preset, en
  Button button_2 (.out(button_2_out));
  PRINT_UDEC print_udec_1 ();  // open: num, start, CLK, RST, ASCII, Write_ASCII, end
  PRINT_DEC print_dec_1 (
    .num(in_1), .start(button_2_out), .CLK(CLK), .RST(CLR), .ASCII(ASCII), .Write_ASCII(Write_ASCII),
    .END(out_2));
  TTY #(.rows(32), .cols(60)) tty_1 (.data(ASCII), .clk(CLK), .we(Write_ASCII), .clr(CLR));
endmodule

module C_U (
  input  in_1,
  input  in_2,
  input  in_3,
  input  in_4,
  input  in_5,
  input  in_6,
  input  in_7,
  input  in_8,
  output Load_A,
  output Load_B,
  output Load_i,
  output Select_i,
  output Load_j,
  output Select_j,
  output Load_Key,
  output END,
  output Output
);

  wire demultiplexer_1_out0, demultiplexer_1_out1, demultiplexer_2_out0, demultiplexer_2_out1,
       demultiplexer_3_out0, demultiplexer_4_out0, END_0, END_1, END_2, Espera_1_3_q, IDLE_q, Li_2, Lj_2,
       or_1_out, or_3_out, Output_0, While_q, While_True_q;

  D_Flip_Flop IDLE (.clk(in_7), .D(demultiplexer_1_out0), .Q(IDLE_q), .preset(in_8));  // open: Qn, en, reset
  Demultiplexer #(.enable("false")) demultiplexer_1 (
    .out0(demultiplexer_1_out0), .out1(demultiplexer_1_out1), .in(IDLE_q), .sel(in_1));
  D_Flip_Flop Espera_1 (.clk(in_7), .D(demultiplexer_1_out1), .Q(Load_A), .reset(in_8));  // open: Qn, preset, en
  or or_1 (or_1_out, Lj_2, Select_j);
  Demultiplexer #(.enable("false")) demultiplexer_2 (
    .out0(demultiplexer_2_out0), .out1(demultiplexer_2_out1), .in(While_True_q), .sel(in_6));
  D_Flip_Flop While_True (.clk(in_7), .D(or_1_out), .Q(While_True_q), .reset(in_8));  // open: Qn, preset, en
  D_Flip_Flop Espera_1_2 (.clk(in_7), .D(Load_A), .Q(Load_B), .reset(in_8));  // open: Qn, preset, en
  D_Flip_Flop Espera_1_3 (.clk(in_7), .D(Load_B), .Q(Espera_1_3_q), .reset(in_8));  // open: Qn, preset, en
  Demultiplexer #(.enable("false")) demultiplexer_3 (
    .out0(demultiplexer_3_out0), .out1(Li_2), .in(demultiplexer_2_out1), .sel(in_4));
  Demultiplexer #(.enable("false")) demultiplexer_4 (
    .out0(demultiplexer_4_out0), .out1(Select_i), .in(Espera_1_3_q), .sel(in_2));
  or or_2 (END_1, END_0, demultiplexer_4_out0);
  Demultiplexer #(.enable("false")) demultiplexer_5 (.out0(Lj_2), .out1(END_0), .in(demultiplexer_3_out0), .sel(in_5));
  not not_1 (Output_0, END_1);
  or or_3 (or_3_out, Select_i, Li_2);
  D_Flip_Flop While (.clk(in_7), .D(or_3_out), .Q(While_q), .reset(in_8));  // open: Qn, preset, en
  Demultiplexer #(.enable("false")) demultiplexer_6 (.out0(END_2), .out1(Load_Key), .in(While_q), .sel(in_3));
  D_Flip_Flop Espera_1_4 (.clk(in_7), .D(Load_Key), .Q(Select_j), .reset(in_8));  // open: Qn, preset, en
  or or_4 (Load_i, Select_i, Li_2);
  or or_5 (Load_j, Select_j, Lj_2);
  or or_6 (END, END_1, END_2);
  or or_7 (Output, Output_0, END_2);

  // Other names for the same wires on the sheet: A__B = in_2; CLK = in_7; CLR = in_8; i__A = in_3; J__A_B_1 = in_6;
  //   J__A_B_1_t = in_5; Key____Input__J = in_4; LA = Load_A; LB = Load_B; LKey = Load_Key; Output_1 = END_2;
  //   Li_1 = Select_i; Si = Select_i; Lj_1 = Select_j; Sj = Select_j; Start = in_1; while = Li_2
endmodule

module D_P (
  input  in_1,
  input  in_2,
  input  in_3,
  input  in_4,
  input  in_5,
  input  in_6,
  input  in_7,
  input  [31:0] in_8,
  input  in_9,
  input  in_10,
  output out_11,
  output out_12,
  output out_13,
  output out_14,
  output out_15,
  output [23:0] Dir_Input
);

  wire comparator_2_lt, comparator_3_eq, comparator_3_lt;
  wire [23:0] multiplexer_3_out, multiplexer_4_out;
  wire [31:0] A, A_1, A_2, A_B_1, B, i, i_plus_plus, j, j_plus_plus, Key, multiplexer_1_out,
       multiplexer_2_out;

  Comparator #(.width(32), .mode("unsigned")) comparator_1 (.a(A), .b(B), .eq(out_11));  // open: gt, lt
  Comparator #(.width(32), .mode("unsigned")) comparator_2 (
    .a(j), .b(A_B_1), .eq(out_14), .lt(comparator_2_lt));  // open: gt
  Comparator #(.width(32), .mode("unsigned")) comparator_3 (
    .a(i), .b(A), .eq(comparator_3_eq), .lt(comparator_3_lt));  // open: gt
  Comparator #(.width(32), .mode("unsigned")) comparator_4 (.a(Key), .b(in_8), .eq(out_13));  // open: gt, lt
  or or_1 (out_15, out_14, comparator_2_lt);
  or or_2 (out_12, comparator_3_eq, comparator_3_lt);
  Register #(.width(32)) register_1 (.D(in_8), .en(in_1), .Q(A), .clk(in_9), .clr(in_10));
  Register #(.width(32)) register_2 (.D(in_8), .en(in_2), .Q(B), .clk(in_9), .clr(in_10));
  Register #(.width(32)) register_3 (.D(in_8), .en(in_5), .Q(Key), .clk(in_9), .clr(in_10));
  Adder #(.width(32)) adder_1 (.a(A), .b(32'h1), .out(A_1));  // open: cin, cout
  Adder #(.width(32)) adder_2 (.a(A), .b(32'h2), .out(A_2));  // open: cin, cout
  Adder #(.width(32)) adder_3 (.a(i), .b(32'h1), .out(i_plus_plus));  // open: cin, cout
  Adder #(.width(32)) adder_4 (.a(j), .b(32'h1), .out(j_plus_plus));  // open: cin, cout
  Multiplexer #(.width(32), .enable("false")) multiplexer_1 (
    .in0(i_plus_plus), .in1(32'h1), .out(multiplexer_1_out), .sel(in_4));
  Multiplexer #(.width(32), .enable("false")) multiplexer_2 (
    .in0(j_plus_plus), .in1(A_2), .out(multiplexer_2_out), .sel(in_7));
  Register #(.width(32)) register_4 (.D(multiplexer_1_out), .en(in_3), .Q(i), .clk(in_9), .clr(in_10));
  Register #(.width(32)) register_5 (.D(multiplexer_2_out), .en(in_6), .Q(j), .clk(in_9), .clr(in_10));
  Adder #(.width(32)) adder_5 (.a(A_1), .b(B), .out(A_B_1));  // open: cin, cout
  Multiplexer #(.width(24), .enable("false")) multiplexer_3 (
    .in0(j[23:0]), .in1(i[23:0]), .out(multiplexer_3_out), .sel(in_5));
  Multiplexer #(.width(24), .enable("false")) multiplexer_4 (
    .in0(multiplexer_3_out), .in1(A_1[23:0]), .out(multiplexer_4_out), .sel(in_2));
  Multiplexer #(.width(24), .enable("false")) multiplexer_5 (
    .in0(multiplexer_4_out), .in1({24{1'b0}}), .out(Dir_Input), .sel(in_1));

  // Other names for the same wires on the sheet: A__B = out_11; CLK = in_9; CLR = in_10; Data_Input[31:0] = in_8;
  //   i__A = out_12; j__A_B_1 = out_15; j__A_B_1_t = out_14; Key___Input__j = out_13; LA = in_1; LB = in_2; Li = in_3;
  //   Lj = in_6; LKey = in_5; Si = in_4; Sj = in_7
endmodule
