// Logisim project BigASM.circ as structural Verilog
module BOARD_BIG_ASM (
  output out_1
);

  wire button_1_out, CLK, CLR, d_ff_1_q, not_1_out, Write, Write_ASCII;
  wire [6:0] ASCII;
  wire [7:0] counter_1_q;
  wire [23:0] Dir_INPUT, Dir_MEMORY;
  wire [31:0] INPUT, MEMORY_IN, MEMORY_OUT;

  Button button_1 (.out(button_1_out));
  Clock clock_1 (.out(CLK));
  D_Flip_Flop d_ff_1 (.clk(CLK), .D(1'b1), .Q(d_ff_1_q), .reset(button_1_out));  // open: Qn, preset, en
  D_Flip_Flop d_ff_2 (.clk(CLK), .D(d_ff_1_q), .Qn(CLR), .reset(button_1_out));  // open: Q, preset, en
  BIG_ASM big_asm_1 (
    .DATA_INPUT(INPUT), .MEMORY_IN(MEMORY_OUT), .CLK(CLK), .CLR(CLR), .DIR_INPUT(Dir_INPUT),
    .MEMORY_OUT(MEMORY_IN), .DIR_MEMORY(Dir_MEMORY), .Write_OUTPUT(Write), .ASCII(ASCII),
    .Write_ASCII(Write_ASCII), .END(out_1));
  MEMORY memory_1 (.DIR(Dir_MEMORY), .DATA_IN(MEMORY_IN), .WRITE(Write), .CLK(CLK), .CLR(CLR), .DATA_OUT(MEMORY_OUT));
  INPUT input_1 (.DIR(Dir_INPUT), .CLK(CLK), .DATA_OUT(INPUT));
  Counter counter_1 (.load(1'b0), .count(not_1_out), .Q(counter_1_q), .clk(CLK), .clr(CLR));  // open: D, carry
  not not_1 (not_1_out, out_1);
  // Probe on counter_1_q
  TTY #(.rows(32), .cols(60)) tty_1 (.data(ASCII), .clk(CLK), .we(Write_ASCII), .clr(CLR));

  // Other names for the same wires on the sheet: END = out_1

  // Notes on the sheet:
  //   COUNTER
  //   BOARD
endmodule

module INPUT (
  input  [23:0] DIR,
  input  CLK,
  output [31:0] DATA_OUT
);

  RAM #(.addrWidth(24), .dataWidth(32)) ram_1 (.addr(DIR), .data(DATA_OUT), .clk(CLK), .ld(1'b1));  // open: sel, clr
endmodule

module MEMORY (
  input  [23:0] DIR,
  input  [31:0] DATA_IN,
  input  WRITE,
  input  CLK,
  input  CLR,
  output [31:0] DATA_OUT
);

  RAM #(.addrWidth(24), .dataWidth(32), .bus("separate")) ram_1 (
    .addr(DIR), .din(DATA_IN), .data(DATA_OUT), .str(WRITE), .clk(CLK), .clr(CLR));  // open: sel, ld
endmodule

module BIG_ASM (
  input  [31:0] DATA_INPUT,
  input  [31:0] MEMORY_IN,
  input  CLK,
  input  CLR,
  output [23:0] DIR_INPUT,
  output [31:0] MEMORY_OUT,
  output [23:0] DIR_MEMORY,
  output Write_OUTPUT,
  output [6:0] ASCII,
  output Write_ASCII,
  output END
);

  wire CA, d_ff_1_q, I__M_N_1_M, J__M, K__M_N_1, LI, LJ, LJ_0, LK, LK_0, LM, LN, LP, or_1_out, or_2_out,
       or_3_out, SI, SJ, SJ_0, SP, Start, Start2;
  wire [31:0] P;

  D_Flip_Flop d_ff_1 (.clk(CLK), .D(1'b0), .Q(d_ff_1_q), .preset(CLR));  // open: Qn, en, reset
  or or_1 (or_1_out, LJ, LJ_0);
  or or_2 (or_2_out, LK, LK_0);
  D_Flip_Flop d_ff_2 (.clk(CLK), .D(d_ff_1_q), .Q(Start), .reset(CLR));  // open: Qn, preset, en
  or or_3 (or_3_out, SJ, SJ_0);
  COPY_V copy_v_1 (
    .in_1(Start), .in_2(I__M_N_1_M), .in_3(CLK), .in_4(CLR), .out_5(LN), .out_6(LM), .out_7(LK_0),
    .out_8(LI), .out_9(SI), .out_10(LJ_0), .out_13(Write_OUTPUT), .out_14(Start2), .out_12(CA), .out_11(SJ_0));
  D_P d_p_1 (
    .in_1(LN), .in_2(LM), .in_3(LI), .in_4(SI), .in_5(or_1_out), .in_6(or_3_out), .in_7(or_2_out), .in_8(LP),
    .in_9(SP), .in_10(CA), .in_11(CLK), .in_12(CLR), .in_13(DATA_INPUT), .in_14(MEMORY_IN),
    .out_15(I__M_N_1_M), .out_16(K__M_N_1), .out_17(J__M), .out_18(P), .out_19(DIR_INPUT), .out_20(DIR_MEMORY));
  C_U c_u_1 (
    .in_1(Start2), .in_2(K__M_N_1), .in_3(J__M), .in_4(P), .in_5(CLK), .in_6(CLR), .out_7(LJ), .out_8(SJ),
    .out_9(LK), .out_10(LP), .out_11(SP), .out_12(Write_ASCII), .out_13(ASCII), .out_14(END));

  assign MEMORY_OUT = DATA_INPUT;

  // Other names for the same wires on the sheet: DI[31:0] = DATA_INPUT; DirI[23:0] = DIR_INPUT;
  //   DirM[23:0] = DIR_MEMORY; MI[31:0] = MEMORY_IN; W_O = Write_OUTPUT; WA = Write_ASCII
endmodule

module PRINT_UDEC (
  input  [31:0] num,
  input  start,
  input  CLK,
  input  RST,
  output [6:0] ASCII,
  output Write_ASCII,
  output \end 
);

  wire _0_c, _0_n, demultiplexer_1_out0, demultiplexer_2_out0, demultiplexer_2_out1, demultiplexer_3_out0,
       demultiplexer_3_out1, IDLE_2_q, IDLE_3_q, IDLE_4_q, IDLE_q, Lc, Lc_0, Ln, Ln_0, or_1_out;
  wire [23:0] bit_extender_1_out;
  wire [31:0] c, c___1, c___1_t, divider_1_rem, memory_1_data_out, multiplexer_1_out, multiplexer_2_out,
       multiplexer_3_out, n, n___10, n___10___48;

  Multiplexer #(.width(32), .enable("false")) multiplexer_1 (
    .in0(num), .in1(n___10), .out(multiplexer_1_out), .sel(Lc_0));
  Divider #(.width(32)) divider_1 (.a(n), .b(32'ha), .out(n___10), .rem(divider_1_rem));  // open: upper
  Adder #(.width(32)) adder_1 (.a(divider_1_rem), .b(32'h30), .out(n___10___48));  // open: cin, cout
  or or_1 (or_1_out, demultiplexer_1_out0, \end );
  Register #(.width(32)) u_n (.D(multiplexer_1_out), .en(Ln), .Q(n), .clk(CLK), .clr(RST));
  D_Flip_Flop IDLE (.clk(CLK), .D(or_1_out), .Q(IDLE_q), .preset(RST));  // open: Qn, en, reset
  Demultiplexer #(.enable("false")) demultiplexer_1 (
    .out0(demultiplexer_1_out0), .out1(Ln_0), .in(IDLE_q), .sel(start));
  or or_2 (Write_ASCII, demultiplexer_3_out0, demultiplexer_2_out1);
  Multiplexer #(.width(32), .enable("false")) multiplexer_2 (
    .in0(c___1), .in1(c___1_t), .out(multiplexer_2_out), .sel(Write_ASCII));
  Adder #(.width(32)) adder_2 (.a(c), .b(32'h1), .out(c___1));  // open: cin, cout
  Subtractor #(.width(32)) subtractor_1 (.a(c), .b(32'h1), .out(c___1_t));  // open: bin, bout
  D_Flip_Flop IDLE_2 (.clk(CLK), .D(Ln_0), .Q(IDLE_2_q), .reset(RST));  // open: Qn, preset, en
  Register #(.width(32)) u_c (.D(multiplexer_2_out), .en(Lc), .Q(c), .clk(CLK), .clr(RST));
  or or_3 (Lc_0, IDLE_2_q, demultiplexer_3_out1);
  Multiplexer #(.width(32), .enable("false")) multiplexer_3 (
    .in0(c), .in1(c___1_t), .out(multiplexer_3_out), .sel(Write_ASCII));
  Comparator #(.width(32), .mode("unsigned")) comparator_1 (.a({32{1'b0}}), .b(n), .lt(_0_n));  // open: gt, eq
  Comparator #(.width(32), .mode("unsigned")) comparator_2 (.a({32{1'b0}}), .b(c), .lt(_0_c));  // open: gt, eq
  D_Flip_Flop IDLE_3 (.clk(CLK), .D(Write_ASCII), .Q(IDLE_3_q), .reset(RST));  // open: Qn, preset, en
  Demultiplexer #(.enable("false")) demultiplexer_2 (
    .out0(demultiplexer_2_out0), .out1(demultiplexer_2_out1), .in(IDLE_3_q), .sel(_0_c));
  Bit_Extender #(.in_width(32), .out_width(24)) bit_extender_1 (.in(multiplexer_3_out), .out(bit_extender_1_out));
  D_Flip_Flop IDLE_4 (.clk(CLK), .D(Lc_0), .Q(IDLE_4_q), .reset(RST));  // open: Qn, preset, en
  or or_4 (Lc, Lc_0, Write_ASCII);
  or or_5 (Ln, Ln_0, Lc_0);
  Demultiplexer #(.enable("false")) demultiplexer_3 (
    .out0(demultiplexer_3_out0), .out1(demultiplexer_3_out1), .in(IDLE_4_q), .sel(_0_n));
  D_Flip_Flop IDLE_5 (.clk(CLK), .D(demultiplexer_2_out0), .Q(\end ), .reset(RST));  // open: Qn, preset, en
  MEMORY memory_1 (
    .DIR(bit_extender_1_out), .DATA_IN(n___10___48), .WRITE(Lc_0), .CLK(CLK), .CLR(RST),
    .DATA_OUT(memory_1_data_out));
  Bit_Extender #(.in_width(32), .out_width(7)) bit_extender_2 (.in(memory_1_data_out), .out(ASCII));

  // Other names for the same wires on the sheet: Lc_1 = Write_ASCII; Sc = Write_ASCII; Ln_1 = Lc_0; Sn = Lc_0;
  //   Write = Lc_0
endmodule

module PRINT_DEC (
  input  [31:0] num,
  input  start,
  input  CLK,
  input  RST,
  output [6:0] ASCII,
  output Write_ASCII,
  output END
);

  wire demultiplexer_1_out0, demultiplexer_1_out1, demultiplexer_2_out0, demultiplexer_3_out0, end_t,
       IDLE_3_q, IDLE_q, or_1_out, or_2_out, or_3_out, S_ASCII, startUDEC, Write_ASCII_1;
  wire [6:0] ASCII_t;
  wire [31:0] multiplexer_1_out, negator_1_out;

  or or_1 (or_1_out, demultiplexer_1_out0, END);
  Negator #(.width(32)) negator_1 (.in(num), .out(negator_1_out));
  D_Flip_Flop IDLE (.clk(CLK), .D(or_1_out), .Q(IDLE_q), .preset(RST));  // open: Qn, en, reset
  Demultiplexer #(.enable("false")) demultiplexer_1 (
    .out0(demultiplexer_1_out0), .out1(demultiplexer_1_out1), .in(IDLE_q), .sel(start));
  Multiplexer #(.width(32), .enable("false")) multiplexer_1 (
    .in0(num), .in1(negator_1_out), .out(multiplexer_1_out), .sel(num[31]));
  Demultiplexer #(.enable("false")) demultiplexer_2 (
    .out0(demultiplexer_2_out0), .out1(S_ASCII), .in(demultiplexer_1_out1), .sel(num[31]));
  or or_2 (or_2_out, demultiplexer_2_out0, S_ASCII);
  D_Flip_Flop IDLE_2 (.clk(CLK), .D(or_2_out), .Q(startUDEC), .reset(RST));  // open: Qn, preset, en
  PRINT_UDEC print_udec_1 (
    .num(multiplexer_1_out), .start(startUDEC), .CLK(CLK), .RST(RST), .ASCII(ASCII_t),
    .Write_ASCII(Write_ASCII_1), .\end (end_t));
  D_Flip_Flop IDLE_3 (.clk(CLK), .D(or_3_out), .Q(IDLE_3_q), .reset(RST));  // open: Qn, preset, en
  or or_3 (or_3_out, startUDEC, demultiplexer_3_out0);
  Demultiplexer #(.enable("false")) demultiplexer_3 (
    .out0(demultiplexer_3_out0), .out1(END), .in(IDLE_3_q), .sel(end_t));
  Multiplexer #(.width(7), .enable("false")) multiplexer_2 (
    .in0(ASCII_t), .in1(7'b0101101), .out(ASCII), .sel(S_ASCII));
  or or_4 (Write_ASCII, S_ASCII, Write_ASCII_1);

  // Other names for the same wires on the sheet: sign = num[31]; Write_ASCII_0 = S_ASCII
endmodule

module TEST_PRINT (
  input  [31:0] in_1,
  output out_2
);

  wire button_1_out, button_2_out, CLK, CLR, d_ff_1_q, Write_ASCII;
  wire [6:0] ASCII;

  Button button_1 (.out(button_1_out));
  Clock clock_1 (.out(CLK));
  D_Flip_Flop d_ff_1 (.clk(CLK), .D(1'b1), .Q(d_ff_1_q), .reset(button_1_out));  // open: Qn, preset, en
  D_Flip_Flop d_ff_2 (.clk(CLK), .D(d_ff_1_q), .Qn(CLR), .reset(button_1_out));  // open: Q, preset, en
  Button button_2 (.out(button_2_out));
  PRINT_UDEC print_udec_1 ();  // open: num, start, CLK, RST, ASCII, Write_ASCII, end
  PRINT_DEC print_dec_1 (
    .num(in_1), .start(button_2_out), .CLK(CLK), .RST(CLR), .ASCII(ASCII), .Write_ASCII(Write_ASCII),
    .END(out_2));
  TTY #(.rows(32), .cols(60)) tty_1 (.data(ASCII), .clk(CLK), .we(Write_ASCII), .clr(CLR));
endmodule

// ASCII
module C_U (
  input  in_1,
  input  in_2,
  input  in_3,
  input  [31:0] in_4,
  input  in_5,
  input  in_6,
  output out_7,
  output out_8,
  output out_9,
  output out_10,
  output out_11,
  output out_12,
  output [6:0] out_13,
  output out_14
);

  wire d_ff_1_q, d_ff_2_q, d_ff_3_q, demultiplexer_1_out0, demultiplexer_2_out0, demultiplexer_2_out1, LJ_1,
       LJ_2, LP_1, or_1_out, print_udec_1_end, WA_1;
  wire [6:0] ASCII;

  Demultiplexer #(.enable("false")) demultiplexer_1 (
    .out0(demultiplexer_1_out0), .out1(LJ_1), .in(d_ff_1_q), .sel(in_1));
  D_Flip_Flop d_ff_1 (.clk(in_5), .D(demultiplexer_1_out0), .Q(d_ff_1_q), .preset(in_6));  // open: Qn, en, reset
  D_Flip_Flop d_ff_2 (.clk(in_5), .D(LJ_2), .Q(d_ff_2_q), .reset(in_6));  // open: Qn, preset, en
  Demultiplexer #(.enable("false")) demultiplexer_2 (
    .out0(demultiplexer_2_out0), .out1(demultiplexer_2_out1), .in(d_ff_2_q), .sel(in_3));
  or or_1 (or_1_out, LJ_1, demultiplexer_2_out0, out_11);
  D_Flip_Flop d_ff_3 (.clk(in_5), .D(or_1_out), .Q(d_ff_3_q), .reset(in_6));  // open: Qn, preset, en
  Demultiplexer #(.enable("false")) demultiplexer_3 (.out0(out_14), .out1(LP_1), .in(d_ff_3_q), .sel(in_2));
  PRINT_UDEC print_udec_1 (
    .num(in_4), .start(demultiplexer_2_out1), .CLK(in_5), .RST(in_6), .ASCII(ASCII), .Write_ASCII(WA_1),
    .\end (print_udec_1_end));
  D_Flip_Flop d_ff_4 (.clk(in_5), .D(print_udec_1_end), .Q(out_11), .reset(in_6));  // open: Qn, preset, en
  D_Flip_Flop d_ff_5 (.clk(in_5), .D(LP_1), .Q(LJ_2), .reset(in_6));  // open: Qn, preset, en
  or or_2 (out_7, LJ_1, LJ_2, out_11);
  or or_3 (out_8, LJ_1, out_11);
  or or_4 (out_9, LJ_1, LJ_2);
  or or_5 (out_10, LP_1, out_11);
  or or_6 (out_12, WA_1, out_11);
  Multiplexer #(.width(7), .enable("false")) multiplexer_1 (.in0(7'b0100000), .in1(ASCII), .out(out_13), .sel(WA_1));

  // Other names for the same wires on the sheet: CLK = in_5; CLR = in_6; END = out_14; J__M = in_3; K__N_M_1 = in_2;
  //   LK_2 = LJ_2; P[31:0] = in_4; LK_1 = LJ_1; SJ_1 = LJ_1; Start = in_1; LJ_3 = out_11; LP_2 = out_11;
  //   SJ_2 = out_11; SP = out_11; WA_2 = out_11; while = out_11
endmodule

module D_P (
  input  in_1,
  input  in_2,
  input  in_3,
  input  in_4,
  input  in_5,
  input  in_6,
  input  in_7,
  input  in_8,
  input  in_9,
  input  in_10,
  input  in_11,
  input  in_12,
  input  [31:0] in_13,
  input  [31:0] in_14,
  output out_15,
  output out_16,
  output out_17,
  output [31:0] out_18,
  output [23:0] out_19,
  output [23:0] out_20
);

  wire comparator_1_eq, comparator_1_lt, comparator_2_eq, comparator_2_lt, comparator_3_lt;
  wire [31:0] I, I_plus_plus, J_plus_plus, K, K_plus_plus, M, multiplexer_1_out, multiplexer_2_out,
       multiplexer_3_out, multiplier_1_out, multiplier_2_out, N, N_M_1, N_M_1_M, N_M_2, P__M_j__N_i;
  wire [31:24] J;

  Multiplier #(.width(32)) multiplier_1 (.a(N), .b(M), .out(multiplier_1_out));  // open: cin, cout
  Register #(.width(32)) register_1 (.D(in_13), .en(in_1), .Q(N), .clk(in_11), .clr(in_12));
  Register #(.width(32)) register_2 (.D(in_13), .en(in_2), .Q(M), .clk(in_11), .clr(in_12));
  Adder #(.width(32)) adder_1 (.a(I), .b(32'h1), .out(I_plus_plus));  // open: cin, cout
  Adder #(.width(32)) adder_2 (.a({J, out_20}), .b(32'h1), .out(J_plus_plus));  // open: cin, cout
  Adder #(.width(32)) adder_3 (.a(K), .b(32'h1), .out(K_plus_plus));  // open: cin, cout
  Adder #(.width(32)) adder_4 (.a(32'h2), .b(multiplier_1_out), .out(N_M_2));  // open: cin, cout
  Adder #(.width(32)) adder_5 (.a(multiplier_1_out), .b(32'h1), .out(N_M_1));  // open: cin, cout
  Multiplexer #(.width(32), .enable("false")) multiplexer_1 (
    .in0(I_plus_plus), .in1(N_M_2), .out(multiplexer_1_out), .sel(in_4));
  Multiplexer #(.width(32), .enable("false")) multiplexer_2 (
    .in0(J_plus_plus), .in1({32{1'b0}}), .out(multiplexer_2_out), .sel(in_6));
  Adder #(.width(32)) adder_6 (.a(N_M_1), .b(M), .out(N_M_1_M));  // open: cin, cout
  Register #(.width(32)) register_3 (.D(multiplexer_1_out), .en(in_3), .Q(I), .clk(in_11), .clr(in_12));
  Register #(.width(32)) register_4 (.D(multiplexer_2_out), .en(in_5), .Q({J, out_20}), .clk(in_11), .clr(in_12));
  Comparator #(.width(32), .mode("unsigned")) comparator_1 (
    .a(I), .b(N_M_1_M), .eq(comparator_1_eq), .lt(comparator_1_lt));  // open: gt
  or or_1 (out_15, comparator_1_eq, comparator_1_lt);
  Comparator #(.width(32), .mode("unsigned")) comparator_2 (
    .a(K), .b(N_M_1), .eq(comparator_2_eq), .lt(comparator_2_lt));  // open: gt
  or or_2 (out_16, comparator_2_eq, comparator_2_lt);
  Comparator #(.width(32), .mode("unsigned")) comparator_3 (
    .a({J, out_20}), .b(M), .eq(out_17), .lt(comparator_3_lt));  // open: gt
  Multiplier #(.width(32)) multiplier_2 (.a(in_13), .b(in_14), .out(multiplier_2_out));  // open: cin, cout
  Multiplexer #(.width(32), .enable("false")) multiplexer_3 (
    .in0(P__M_j__N_i), .in1({32{1'b0}}), .out(multiplexer_3_out), .sel(in_9));
  Adder #(.width(32)) adder_7 (.a(multiplier_2_out), .b(out_18), .out(P__M_j__N_i));  // open: cin, cout
  Register #(.width(32)) register_5 (.D(multiplexer_3_out), .en(in_8), .Q(out_18), .clk(in_11), .clr(in_12));
  Register #(.width(32)) register_6 (.D(K_plus_plus), .en(in_7), .Q(K), .clk(in_11), .clr(in_12));
  Multiplexer #(.width(24), .enable("false")) multiplexer_4 (.in0(K[23:0]), .in1(I[23:0]), .out(out_19), .sel(in_10));

  // Other names for the same wires on the sheet: CA = in_10; CLK = in_11; CLR = in_12; DI[31:0] = in_13;
  //   i__N_M_1_M = out_15; J[23:0] = out_20; J__M = out_17; K__N_M_1 = out_16; LI = in_3; LJ = in_5; LK = in_7;
  //   LM = in_2; LN = in_1; LP = in_8; MI[31:0] = in_14; P[31:0] = out_18; SI = in_4; SJ = in_6; SP = in_9

  // Notes on the sheet:
  //   DIR_INPUT
  //   DIR_MEMORY
endmodule

module COPY_V (
  input  in_1,
  input  in_2,
  input  in_3,
  input  in_4,
  output out_5,
  output out_6,
  output out_7,
  output out_8,
  output out_9,
  output out_10,
  output out_11,
  output out_12,
  output out_13,
  output out_14
);

  wire d_ff_1_q, d_ff_5_q, d_ff_6_q, demultiplexer_1_out0;

  D_Flip_Flop d_ff_1 (.clk(in_3), .D(demultiplexer_1_out0), .Q(d_ff_1_q), .preset(in_4));  // open: Qn, en, reset
  Demultiplexer #(.enable("false")) demultiplexer_1 (
    .out0(demultiplexer_1_out0), .out1(out_5), .in(d_ff_1_q), .sel(in_1));
  D_Flip_Flop d_ff_2 (.clk(in_3), .D(out_5), .Q(out_7), .reset(in_4));  // open: Qn, preset, en
  D_Flip_Flop d_ff_3 (.clk(in_3), .D(out_7), .Q(out_6), .reset(in_4));  // open: Qn, preset, en
  D_Flip_Flop d_ff_4 (.clk(in_3), .D(out_6), .Q(out_9), .reset(in_4));  // open: Qn, preset, en
  or or_1 (out_8, out_9, d_ff_6_q);
  D_Flip_Flop d_ff_5 (.clk(in_3), .D(out_8), .Q(d_ff_5_q), .reset(in_4));  // open: Qn, preset, en
  Demultiplexer #(.enable("false")) demultiplexer_2 (.out0(out_14), .out1(out_12), .in(d_ff_5_q), .sel(in_2));
  D_Flip_Flop d_ff_6 (.clk(in_3), .D(out_12), .Q(d_ff_6_q), .reset(in_4));  // open: Qn, preset, en

  assign out_10 = out_8;
  assign out_11 = out_9;
  assign out_13 = out_12;

  // Other names for the same wires on the sheet: CLK = in_3; CLR = in_4; END = out_14; I__N_M_1_M = in_2; LI = out_8;
  //   LJ = out_8; LK = out_7; LM = out_6; LN = out_5; SI = out_9; SJ = out_9; Start = in_1; CA = out_12; W_M = out_12
endmodule
